// Logisim project Lab 2.circ as structural Verilog: 1 circuit, main circuit main
module main (
  input  D,
  input  P,
  input  T,
  input  E,
  output out_5
);

  wire and_1_out, and_2_out, not_1_out, not_2_out;

  not not_1 (not_1_out, T);
  not not_2 (not_2_out, E);
  and and_1 (and_1_out, D, D, not_2_out, P);
  and and_2 (and_2_out, not_1_out, not_1_out, D, not_2_out);
  or or_1 (out_5, and_1_out, and_2_out);
endmodule
