// Logisim project Lab 4.circ as structural Verilog: 1 circuit, main circuit main
module main (
  output out_1,
  output out_2,
  output out_3,
  output out_4
);

  wire and_1_out, and_2_out, and_3_out, and_4_out, clock_1_out, not_1_out, not_2_out, not_3_out, not_4_out,
       not_5_out, not_6_out, not_7_out, not_8_out, not_9_out, not_10_out, not_11_out, not_12_out;

  not not_1 (not_1_out, out_1);
  not not_2 (not_2_out, out_2);
  not not_3 (not_3_out, out_3);
  not not_4 (not_4_out, out_2);
  not not_5 (not_5_out, out_3);
  not not_6 (not_6_out, out_4);
  not not_7 (not_7_out, out_1);
  not not_8 (not_8_out, out_3);
  not not_9 (not_9_out, out_4);
  not not_10 (not_10_out, out_1);
  not not_11 (not_11_out, out_2);
  not not_12 (not_12_out, out_4);
  and and_1 (and_1_out, not_1_out, not_2_out, not_3_out);
  and and_2 (and_2_out, out_1, not_4_out, not_6_out, not_5_out);
  and and_3 (and_3_out, not_7_out, out_2, not_8_out, not_9_out);
  and and_4 (and_4_out, not_10_out, not_11_out, out_3, not_12_out);
  Clock clock_1 (.out(clock_1_out));
  D_Flip_Flop d_ff_1 (.clk(clock_1_out), .D(and_4_out), .Q(out_4));  // open: Qn, preset, en, reset
  D_Flip_Flop d_ff_2 (.clk(clock_1_out), .D(and_1_out), .Q(out_1));  // open: Qn, preset, en, reset
  D_Flip_Flop d_ff_3 (.clk(clock_1_out), .D(and_2_out), .Q(out_2));  // open: Qn, preset, en, reset
  D_Flip_Flop d_ff_4 (.clk(clock_1_out), .D(and_3_out), .Q(out_3));  // open: Qn, preset, en, reset

  // Notes on the sheet:
  //   A
  //   B
  //   C
  //   D
  //   A'B'CD'
  //   A'B'C'
  //   AB'C'D'
  //   A'BC'D'
endmodule
