// Logisim project circuit one.circ as structural Verilog: 1 circuit, main circuit main
module main (
  input  x,
  input  y,
  output out_3
);

  wire and_1_out, and_2_out, and_3_out, not_1_out, not_2_out;

  not not_1 (not_1_out, x);
  not not_2 (not_2_out, y);
  and and_1 (and_1_out, x, y);
  and and_2 (and_2_out, x, not_2_out);
  and and_3 (and_3_out, not_1_out, y, y);
  or or_1 (out_3, and_1_out, and_2_out, and_3_out);

  // Notes on the sheet:
  //   F{0,1,1,1)
  //   =
  //   OR GATE
  //   F = xy + xy' + x'y
endmodule
